# Fritzing sketch cablage_tank_controle_moteur_video (saved by Fritzing 0.9.3b)
breadboards: 1

parts:
  Composant4 = Arduino Nano (Rev3.0)
  IC2 = L293D [package=THT]
  M3 = DC Motor
  VCC2 = Battery block 9V
  M4 = DC Motor
  Composant5 = Thumb Joystick
  Composant6 = Thumb Joystick

nets:
  GND: Composant4.GND, IC2.0V, VCC2.-, Composant5.GND, Composant6.GND
  N1: Composant4.D3, IC2.In_2
  N2: Composant4.D4, IC2.In_1
  N3: Composant4.D5, IC2.Enable_1
  N4: Composant4.D6, IC2.Enable_2
  N5: Composant4.D7, IC2.In_4
  N6: Composant4.D8, IC2.In_3
  N7: Composant4.VIN, IC2.+Vmotor, IC2.+V, VCC2.+
  VCC: Composant4.5V, Composant5.VCC, Composant6.VCC
  N8: Composant4.A1, Composant6.HORZ
  N9: Composant4.A0, Composant5.HORZ
  N10: IC2.Out_1_(_Controlled_by_Enable_1_), M3.pin_1
  N11: IC2.Out_2_(_Controlled_by_Enable_1_), M3.pin_2
  N12: IC2.Out_3_(_Controlled_by_Enable_2_), M4.pin_2
  N13: IC2.Out_4_(_Controlled_by_Enable_2_), M4.pin_1
